# Fritzing sketch Lab2.6 (saved by Fritzing 0.8.5b)
breadboards: 1

parts:
  LED1 = smd LED [color="Red (635nm)" package="1206 [SMD]"]
  Part1 = Arduino Uno (Rev3)
  LED2 = smd LED [color="Green (570nm)" package="1206 [SMD]"]
  R1 = Resistor [tolerance=±5% resistance=10 package=THT]
  Photoresister = Photocell (LDR) [package=THT]
  R3 = Resistor [tolerance=±5% resistance=560 package=THT]
  R2 = Resistor [tolerance=±5% resistance=560 package=THT]
  potentiometer = Rotary Potentiometer (Small) [maximum_resistance=100kΩ package=THT]

nets (from the schematic view):
  N1: LED1.cathode, R2.Pin_0
  N2: LED1.anode, Part1.D10_PWM/SS
  N3: Part1.A0, R1.Pin_0, Photoresister.pin_1
  N4: Part1.A1, potentiometer.wiper
  N5: Part1.D9_PWM, LED2.anode
  N6: Part1.GND, Photoresister.pin_0, R3.Pin_1, R2.Pin_1, potentiometer.leg2
  N7: Part1.5V, R1.Pin_1, potentiometer.leg1
