# Fritzing sketch Task2.1 (saved by Fritzing 0.8.5b)
breadboards: 1

parts:
  LED2 = smd LED [color="Green (570nm)" package="1206 [SMD]"]
  LED1 = smd LED [color="Red (635nm)" package="1206 [SMD]"]
  LED3 = smd LED [color="Red (635nm)" package="1206 [SMD]"]
  Part1 = Arduino Uno (Rev3)
  R6 = Resistor [tolerance=±5% resistance=10 package=THT]
  R2 = Resistor [tolerance=±5% resistance=220 package=THT]
  LED4 = smd LED [color="Green (570nm)" package="1206 [SMD]"]
  PushSwitch1 = Pushbutton [package="[THT]"]
  TiltSwitch1 = Tilt Switch [package=THT]
  R1 = Resistor [tolerance=±5% resistance=220 package=THT]
  R3 = Resistor [tolerance=±5% resistance=220 package=THT]
  R4 = Resistor [tolerance=±5% resistance=220 package=THT]
  R5 = Resistor [tolerance=±5% resistance=10 package=THT]

nets:
  N1: LED2.cathode, R2.Pin_1
  N2: LED2.anode, Part1.D9_PWM
  N3: LED1.cathode, R1.Pin_1
  N4: LED1.anode, Part1.D8
  N5: LED3.cathode, R3.Pin_1
  N6: LED3.anode, Part1.D10_PWM/SS
  N7: Part1.D11_PWM/MOSI, LED4.anode
  N8: Part1.GND, R2.Pin_0, PushSwitch1.Pin_1, PushSwitch1.Pin_2, TiltSwitch1.Pin_2, R1.Pin_0, R3.Pin_0, R4.Pin_0
  N9: Part1.D6_PWM, R6.Pin_0, PushSwitch1.Pin_3, PushSwitch1.Pin_4
  N10: Part1.D7, TiltSwitch1.Pin_1, R5.Pin_0
  N11: Part1.5V, R6.Pin_1, R5.Pin_1
  N12: LED4.cathode, R4.Pin_1
